# Fritzing sketch arduino-snespad (saved by Fritzing 0.7.0b)

parts:
  Arduino1 = Arduino
  J1 = female pin header, 5 pins [form="♀ (female)"]

nets:
  N1: Arduino1.D4, J1.pin1
  N2: Arduino1.D3, J1.pin2
  N3: Arduino1.D2, J1.pin3
  N4: Arduino1.+5V, J1.pin5
  N5: Arduino1.GND, J1.pin4

notes:
  SNES Controller
  white: +5V
  brown: GND
  orange: latch
  yellow: clock
  red: data
